# Fritzing sketch gpio-fan (saved by Fritzing 0.9.3b)
breadboards: 1

parts:
  M1 = DC Motor
  Raspberry_Pi_1 = Raspberry Pi 3 [part_number=RPI-3-V1.2]
  Q1 = NPN-Transistor [package="TO92 [THT]"]

nets:
  N1: M1.pin_1, Raspberry_Pi_1.5V
  N2: M1.pin_2, Q1.C
  N3: Raspberry_Pi_1.GPIO14, Q1.B
  N4: Raspberry_Pi_1.GND, Q1.E
